// Logisim project ciruit.circ as structural Verilog
// XOR
module MiXOR (
  input  A,
  input  B,
  output C
);

  wire and_1_out, and_2_out, not_1_out, not_2_out;

  not not_1 (not_1_out, B);
  not not_2 (not_2_out, A);
  and and_1 (and_1_out, A, not_1_out);
  and and_2 (and_2_out, not_2_out, B);
  or or_1 (C, and_1_out, and_2_out);

  // Notes on the sheet:
  //   CP1-EJ1-a
  //   C = (A ∧ ¬B) ∨ (¬A ∧ B)
endmodule

module TestMiXOR (
  input  in_1,
  input  in_2,
  input  in_3,
  input  in_4,
  output out_5,
  output out_6
);

  MiXOR mixor_1 (.A(in_1), .B(in_2), .C(out_5));
  xor xor_1 (out_6, in_3, in_4);

  // Notes on the sheet:
  //   XOR creado por mi
  //   XOR de Logisim
endmodule

module MiSumador (
  input  [3:0] in_1,
  input  [3:0] in_2,
  output [3:0] out_3,
  output [4:0] out_4
);

  // Probe on in_1
  // Probe on in_2
  Adder #(.width(4)) adder_1 (.a(in_1), .b(in_2), .out(out_3), .cout(out_4[4]));  // open: cin
  // Probe on out_3
  // Probe on {out_4[4], out_3}

  assign out_4[3:0] = out_3;

  // Other names for the same wires on the sheet: carry = out_4[4]

  // Notes on the sheet:
  //   CP1-EJ1-b
endmodule
