// Logisim project circuito.circ as structural Verilog
module Half_Adder (
  input  A,
  input  B,
  output Sum,
  output Carry
);

  xor xor_1 (Sum, A, B);
  and and_1 (Carry, A, B);

  // Notes on the sheet:
  //   CP1 - EJ2
endmodule

module Test_Half_Adder (
  input  in_1,
  input  in_2,
  output [1:0] out_3
);

  Half_Adder half_adder_1 (.A(in_1), .B(in_2), .Sum(out_3[0]), .Carry(out_3[1]));
  // Probe on out_3
endmodule
