// Logisim project circuito.circ as structural Verilog: 2 circuits, main circuit main
module main (
);
endmodule

module Full_Adder (
  input  A,
  input  B,
  input  Cin,
  output out_4,
  output carry
);

  wire and_1_out, and_2_out, xor_1_out;

  xor xor_1 (xor_1_out, A, B);
  and and_1 (and_1_out, xor_1_out, Cin);
  and and_2 (and_2_out, B, A);
  xor xor_2 (out_4, xor_1_out, Cin);
  or or_1 (carry, and_1_out, and_2_out);

  // Notes on the sheet:
  //   CP1 - EJ 3
  //   sum  = (A ⊕ B) ⊕ Cin
  //   carry = (A ∧ B) ∨ ((A ⊕ B) ∧ Cin)
endmodule
