// Logisim project circuit.circ as structural Verilog: 2 circuits, main circuit main
module main (
  input  \A₀ ,
  input  \B₀ ,
  input  \A₁ ,
  input  \B₁ ,
  input  \A₂ ,
  input  \B₂ ,
  input  in_7,
  input  \A₃ ,
  input  \B₃ ,
  output [4:0] result
);

  wire full_adder_1_carry, full_adder_2_carry, full_adder_3_carry;

  Full_Adder full_adder_1 (.A(\A₀ ), .B(\B₀ ), .Cin(in_7), .out_4(result[0]), .carry(full_adder_1_carry));
  Full_Adder full_adder_2 (.A(\A₁ ), .B(\B₁ ), .Cin(full_adder_1_carry), .out_4(result[1]), .carry(full_adder_2_carry));
  Full_Adder full_adder_3 (.A(\A₂ ), .B(\B₂ ), .Cin(full_adder_2_carry), .out_4(result[2]), .carry(full_adder_3_carry));
  Full_Adder full_adder_4 (.A(\A₃ ), .B(\B₃ ), .Cin(full_adder_3_carry), .out_4(result[3]), .carry(result[4]));

  // Notes on the sheet:
  //   CP1 - Ej 4
endmodule

// +
module Full_Adder (
  input  A,
  input  B,
  input  Cin,
  output out_4,
  output carry
);

  wire and_1_out, and_2_out, xor_1_out;

  xor xor_1 (xor_1_out, A, B);
  and and_1 (and_1_out, xor_1_out, Cin);
  and and_2 (and_2_out, B, A);
  xor xor_2 (out_4, xor_1_out, Cin);
  or or_1 (carry, and_1_out, and_2_out);

  // Notes on the sheet:
  //   sum  = (A ⊕ B) ⊕ Cin
  //   carry = (A ∧ B) ∨ ((A ⊕ B) ∧ Cin)
endmodule
