// Logisim project circuito.circ as structural Verilog
// +
module Full_Adder (
  input  A,
  input  B,
  input  Cin,
  output out_4,
  output carry
);

  wire and_1_out, and_2_out, xor_1_out;

  xor xor_1 (xor_1_out, A, B);
  and and_1 (and_1_out, xor_1_out, Cin);
  and and_2 (and_2_out, B, A);
  xor xor_2 (out_4, xor_1_out, Cin);
  or or_1 (carry, and_1_out, and_2_out);
endmodule

// 4+
module Sumador_4_digitos (
  input  Cin,
  input  [3:0] A,
  input  [3:0] B,
  output [3:0] sum,
  output carry
);

  wire full_adder_1_carry, full_adder_2_carry, full_adder_3_carry;

  Full_Adder full_adder_1 (.A(A[0]), .B(B[0]), .Cin(Cin), .out_4(sum[0]), .carry(full_adder_1_carry));
  Full_Adder full_adder_2 (.A(A[1]), .B(B[1]), .Cin(full_adder_1_carry), .out_4(sum[1]), .carry(full_adder_2_carry));
  Full_Adder full_adder_3 (.A(A[2]), .B(B[2]), .Cin(full_adder_2_carry), .out_4(sum[2]), .carry(full_adder_3_carry));
  Full_Adder full_adder_4 (.A(A[3]), .B(B[3]), .Cin(full_adder_3_carry), .out_4(sum[3]), .carry(carry));

  // Other names for the same wires on the sheet: A₀ = A[0]; A₁ = A[1]; A₂ = A[2]; A₃ = A[3]; B₀ = B[0]; B₁ = B[1];
  //   B₂ = B[2]; B₃ = B[3]
endmodule

module Restador_4_bits (
  input  [3:0] A,
  input  [3:0] B,
  input  Cin,
  output [3:0] Diff,
  output Cout
);

  wire [3:0] not_1_out;

  assign not_1_out = ~B;  // NOT_Gate not_1, 4 bits wide
  // Probe on B
  // Probe on A
  Sumador_4_digitos sumador_4_digitos_1 (.A(A), .B(not_1_out), .Cin(Cin), .sum(Diff), .carry(Cout));
  // Probe on Diff

  // Notes on the sheet:
  //   CP1 - EJ 5
  //   A - B = A + (-B) = A + (¬B + 1)
endmodule
