// Logisim project circuito.circ as structural Verilog: 5 circuits, main circuit main
module main (
  input  [3:0] A,
  input  [3:0] B,
  input  [1:0] Selector,
  output [3:0] Result
);

  // Probe on A
  // Probe on B
  ALU alu_1 (.A(A), .B(B), .Sel(Selector), .Result(Result));
  // Probe on Result

  // Notes on the sheet:
  //   CP1 - Ej6
endmodule

module Full_Adder (
  input  A,
  input  B,
  input  Cin,
  output out_4,
  output carry
);

  wire and_1_out, and_2_out, xor_1_out;

  xor xor_1 (xor_1_out, A, B);
  and and_1 (and_1_out, xor_1_out, Cin);
  and and_2 (and_2_out, B, A);
  xor xor_2 (out_4, xor_1_out, Cin);
  or or_1 (carry, and_1_out, and_2_out);
endmodule

// 4+
module Sumador_4_bits (
  input  Cin,
  input  [3:0] A,
  input  [3:0] B,
  output [3:0] sum,
  output carry
);

  wire full_adder_1_carry, full_adder_2_carry, full_adder_3_carry;

  Full_Adder full_adder_1 (.A(A[0]), .B(B[0]), .Cin(Cin), .out_4(sum[0]), .carry(full_adder_1_carry));
  Full_Adder full_adder_2 (.A(A[1]), .B(B[1]), .Cin(full_adder_1_carry), .out_4(sum[1]), .carry(full_adder_2_carry));
  Full_Adder full_adder_3 (.A(A[2]), .B(B[2]), .Cin(full_adder_2_carry), .out_4(sum[2]), .carry(full_adder_3_carry));
  Full_Adder full_adder_4 (.A(A[3]), .B(B[3]), .Cin(full_adder_3_carry), .out_4(sum[3]), .carry(carry));

  // Other names for the same wires on the sheet: A₀ = A[0]; A₁ = A[1]; A₂ = A[2]; A₃ = A[3]; B₀ = B[0]; B₁ = B[1];
  //   B₂ = B[2]; B₃ = B[3]
endmodule

// 4-
module Restador_4_bits (
  input  [3:0] A,
  input  [3:0] B,
  output [3:0] Diff,
  output Cout
);

  wire [3:0] not_1_out;

  assign not_1_out = ~B;  // NOT_Gate not_1, 4 bits wide
  Sumador_4_bits sumador_4_bits_1 (.A(A), .B(not_1_out), .Cin(1'b1), .sum(Diff), .carry(Cout));
endmodule

module ALU (
  input  [3:0] A,
  input  [3:0] B,
  input  [1:0] Sel,
  output [3:0] Result
);

  wire [3:0] and_1_out, or_1_out, restador_4_bits_1_diff, sumador_4_bits_1_sum;

  Sumador_4_bits sumador_4_bits_1 (.A(A), .B(B), .Cin(1'b0), .sum(sumador_4_bits_1_sum));  // open: carry
  Restador_4_bits restador_4_bits_1 (.A(A), .B(B), .Diff(restador_4_bits_1_diff));  // open: Cout
  assign and_1_out = A & B;  // AND_Gate and_1, 4 bits wide
  assign or_1_out = A | B;  // OR_Gate or_1, 4 bits wide
  Multiplexer #(.select(2), .width(4)) multiplexer_1 (
    .in0(sumador_4_bits_1_sum), .in1(restador_4_bits_1_diff), .in2(and_1_out), .in3(or_1_out), .out(Result),
    .sel(Sel));  // open: en
endmodule
