// Logisim project circuito.circ as structural Verilog: 7 circuits, main circuit main
module main (
  input  A,
  input  B,
  input  C,
  input  D,
  input  E,
  input  F,
  input  G,
  input  H,
  input  Sel1,
  input  Sel2,
  input  Sel3,
  input  in_12,
  input  Sel1_2,
  input  Sel2_2,
  input  Sel3_2,
  output Res,
  output R1,
  output R2,
  output R3,
  output R4,
  output R5,
  output R6,
  output R7,
  output R8
);

  MUX_8 mux_8_1 (
    .A(A), .B(B), .C(C), .D(D), .E(E), .F(F), .G(G), .H(H), .Sel1(Sel1), .Sel2(Sel2), .Sel3(Sel3), .Res(Res));
  DEMUX_8 demux_8_1 (
    .A(in_12), .Sel1(Sel1_2), .Sel2(Sel2_2), .Sel3(Sel3_2), .R1(R1), .R2(R2), .R3(R3), .R4(R4), .R5(R5),
    .R6(R6), .R7(R7), .R8(R8));

  // Notes on the sheet:
  //   CP1 - EJ 7
  //   Multiplexor con 3 selectores
  //   Multiplexor con 3 selectores
endmodule

// M2
module MUX_2 (
  input  A,
  input  B,
  input  Sel,
  output out_4
);

  wire and_1_out, and_2_out, not_1_out;

  and and_1 (and_1_out, A, not_1_out);
  not not_1 (not_1_out, Sel);
  and and_2 (and_2_out, B, Sel);
  or or_1 (out_4, and_1_out, and_2_out);

  // Notes on the sheet:
  //   Multiplexer de 2 a 1
endmodule

// M4
module MUX_4 (
  input  A,
  input  B,
  input  C,
  input  D,
  input  SEL1,
  input  SEL0,
  output out_7
);

  wire mux_2_1_out_4, mux_2_2_out_4;

  MUX_2 mux_2_1 (.A(A), .B(B), .Sel(SEL0), .out_4(mux_2_1_out_4));
  MUX_2 mux_2_2 (.A(C), .B(D), .Sel(SEL0), .out_4(mux_2_2_out_4));
  MUX_2 mux_2_3 (.A(mux_2_1_out_4), .B(mux_2_2_out_4), .Sel(SEL1), .out_4(out_7));

  // Notes on the sheet:
  //   Multiplexer de 4 a 1
endmodule

module MUX_8 (
  input  A,
  input  B,
  input  C,
  input  D,
  input  E,
  input  F,
  input  Sel3,
  input  G,
  input  H,
  input  Sel1,
  input  Sel2,
  output Res
);

  wire mux_4_1_out_7, mux_4_2_out_7;

  MUX_4 mux_4_1 (.A(A), .B(B), .C(C), .D(D), .SEL0(Sel1), .SEL1(Sel2), .out_7(mux_4_1_out_7));
  MUX_4 mux_4_2 (.A(E), .B(F), .C(G), .D(H), .SEL0(Sel1), .SEL1(Sel2), .out_7(mux_4_2_out_7));
  MUX_2 mux_2_1 (.A(mux_4_1_out_7), .B(mux_4_2_out_7), .Sel(Sel3), .out_4(Res));
endmodule

// DEM2
module DEMUX_2 (
  input  A,
  input  Sel1,
  output R1,
  output R2
);

  wire not_1_out;

  not not_1 (not_1_out, Sel1);
  and and_1 (R1, A, not_1_out);
  and and_2 (R2, A, Sel1);

  // Notes on the sheet:
  //   Demultiplexer de 1 a 2
endmodule

// DEM4
module DEMUX_4 (
  input  A,
  input  Sel1,
  input  Sel2,
  output R1,
  output R2,
  output R3,
  output R4
);

  wire and_1_out, and_2_out, not_1_out;

  not not_1 (not_1_out, Sel2);
  and and_1 (and_1_out, A, not_1_out);
  DEMUX_2 demux_2_1 (.A(and_1_out), .Sel1(Sel1), .R1(R1), .R2(R2));
  and and_2 (and_2_out, A, Sel2);
  DEMUX_2 demux_2_2 (.A(and_2_out), .Sel1(Sel1), .R1(R3), .R2(R4));

  // Notes on the sheet:
  //   Demultiplexer de 1 a 4
endmodule

module DEMUX_8 (
  input  A,
  input  Sel1,
  input  Sel2,
  input  Sel3,
  output R1,
  output R2,
  output R3,
  output R4,
  output R5,
  output R6,
  output R7,
  output R8
);

  wire and_1_out, and_2_out, not_1_out;

  and and_1 (and_1_out, A, not_1_out);
  not not_1 (not_1_out, Sel3);
  and and_2 (and_2_out, A, Sel3);
  DEMUX_4 demux_4_1 (.A(and_1_out), .Sel1(Sel1), .Sel2(Sel2), .R1(R1), .R2(R2), .R3(R3), .R4(R4));
  DEMUX_4 demux_4_2 (.A(and_2_out), .Sel1(Sel1), .Sel2(Sel2), .R1(R5), .R2(R6), .R3(R7), .R4(R8));

  // Notes on the sheet:
  //   Demultiplexer de 1 a 8
endmodule
