// Logisim project circuito.circ as structural Verilog: 2 circuits, main circuit main
module main (
  input  A,
  input  B,
  input  C,
  output out_4,
  output out_5,
  output out_6,
  output out_7,
  output out_8,
  output out_9,
  output out_10,
  output out_11
);

  Decoder_8 decoder_8_1 (
    .A(A), .B(B), .C(C), .out_4(out_4), .out_5(out_5), .out_6(out_6), .out_7(out_7), .out_8(out_8),
    .out_9(out_9), .out_10(out_10), .out_11(out_11));

  // Notes on the sheet:
  //   CP1 - Ej 8
endmodule

// Decoder
module Decoder_8 (
  input  A,
  input  B,
  input  C,
  output out_4,
  output out_5,
  output out_6,
  output out_7,
  output out_8,
  output out_9,
  output out_10,
  output out_11
);

  and and_1 (out_4, ~A, ~B, ~C);  // AND_Gate
  and and_2 (out_5, A, ~B, ~C);  // AND_Gate
  and and_3 (out_6, ~A, B, ~C);  // AND_Gate
  and and_4 (out_7, A, B, ~C);  // AND_Gate
  and and_5 (out_8, ~A, ~B, C);  // AND_Gate
  and and_6 (out_9, A, ~B, C);  // AND_Gate
  and and_7 (out_10, ~A, B, C);  // AND_Gate
  and and_8 (out_11, A, B, C);
endmodule
